# Fritzing sketch iRigate (saved by Fritzing 0.7.12b)
breadboards: 1

parts:
  ATMega328 = atmega328 [package=dip]
  C2_22pF = Ceramic Disk Capacitor [package=THT]
  C1_22pF = Ceramic Disk Capacitor [package=THT]
  CC3000 = Adafruit CC3000 WiFi Breakout
  MOSSFET-N = Basic FET N-Channel [package="TO220 [THT]"]
  D_Motor = Rectifier Diode [part_number=1N4001 package="300 mil [THT]"]
  12_VOLTS = Screw terminal - 2 pins [package=THT]
  S_HUMEDAD = Screw terminal - 2 pins [package=THT]
  12v/5v = Voltage Regulator - 5V [package="TO220 [THT]"]
  R_Reset = Resistor [tolerance=±5% resistance=10k package=THT]
  R_MOS = Resistor [tolerance=±5% resistance=10k package=THT]
  R_WL = Resistor [tolerance=±5% resistance=330 package=THT]
  Water_LED = LED - 5mm [color="Red (633nm)" package="5 mm [THT]"]
  R_TL = Resistor [tolerance=±5% resistance=330 package=THT]
  Twitt_LED = LED - 5mm [color="Red (633nm)" package="5 mm [THT]"]
  R_ML = Resistor [tolerance=±5% resistance=330 package=THT]
  Motor_LED = LED - 5mm [color="Red (633nm)" package="5 mm [THT]"]
  XTAL = CRYSTAL - kHz [frequency="16 MHz"]
  MOTOR_AGUA = Screw terminal - 2 pins [package=THT]
  Regulador = Breadboard Trimpot

nets:
  N1: ATMega328.RESET, R_Reset.Pin_1
  N2: ATMega328.D2, R_TL.Pin_0
  N3: ATMega328.D3_(PWM), CC3000.IRQ
  VCC: ATMega328.VCC, ATMega328.AVCC, ATMega328.AREF, CC3000.VIN, 12v/5v.output_voltage, R_Reset.Pin_0, Regulador.PIN1
  N4: ATMega328.GND#7, C2_22pF.pin_0, C1_22pF.pin_0
  N5: ATMega328.XLAT1, C1_22pF.pin_1, XTAL.pin_0
  N6: ATMega328.XLAT2, C2_22pF.pin_1, XTAL.pin_1
  N7: ATMega328.D5_(PWM), CC3000.VBEN
  N8: ATMega328.D6_(PWM), R_WL.Pin_0
  N9: ATMega328.D8, R_ML.Pin_0
  N10: ATMega328.D9_(PWM), MOSSFET-N.gate, R_MOS.Pin_1
  N11: ATMega328.D10_(PWM), CC3000.CS
  N12: ATMega328.D11_(PWM), CC3000.MOSI
  N13: ATMega328.D12, CC3000.MISO
  N14: ATMega328.D13, CC3000.CLK
  GND: ATMega328.GND#21, CC3000.GND, MOSSFET-N.source, D_Motor.cathode, 12_VOLTS.pin2, 12v/5v.GND, R_MOS.Pin_0, Water_LED.cathode, Twitt_LED.cathode, Motor_LED.cathode, MOTOR_AGUA.pin1, Regulador.PIN3
  N15: ATMega328.A3, S_HUMEDAD.pin2
  N16: ATMega328.A4, Regulador.PIN2
  N17: ATMega328.A5, S_HUMEDAD.pin1
  N18: MOSSFET-N.drain, D_Motor.anode, MOTOR_AGUA.pin2
  N19: 12_VOLTS.pin1, 12v/5v.input_voltage
  N20: R_WL.Pin_1, Water_LED.anode
  N21: R_TL.Pin_1, Twitt_LED.anode
  N22: R_ML.Pin_1, Motor_LED.anode

custom parts:
  Adafruit CC3000 WiFi Breakout: CC3000 WiFi Breakout
